// Logisim project TrabalhoCircuitos.circ as structural Verilog: 4 circuits, main circuit main
module main (
  input  Te1,
  input  Pa1,
  input  Pe1,
  input  Te2,
  input  Pa2,
  input  Pe2
);

  wire cod_1_out_4, cod_1_out_5, cod_2_out_4, cod_2_out_5, dec_1_empateouinvalido, dec_1_j1, dec_1_j2,
       sol_1_out_5, sol_1_out_6;

  cod cod_1 (.Te(Te1), .Pa(Pa1), .Pe(Pe1), .out_4(cod_1_out_4), .out_5(cod_1_out_5));
  cod cod_2 (.Te(Te2), .Pa(Pa2), .Pe(Pe2), .out_4(cod_2_out_4), .out_5(cod_2_out_5));
  SOL sol_1 (
    .j10(cod_1_out_4), .j11(cod_1_out_5), .j20(cod_2_out_4), .j21(cod_2_out_5), .out_5(sol_1_out_5),
    .out_6(sol_1_out_6));
  dec dec_1 (
    .in_1(sol_1_out_5), .in_2(sol_1_out_6), .J1(dec_1_j1), .J2(dec_1_j2),
    .EmpateOuInvalido(dec_1_empateouinvalido));
  LED led_1 (.in(dec_1_j1));
  LED led_2 (.in(dec_1_j2));
  LED led_3 (.in(dec_1_empateouinvalido));
endmodule

module SOL (
  input  j10,
  input  j11,
  input  j20,
  input  j21,
  output out_5,
  output out_6
);

  wire and_1_out, and_2_out, and_3_out, and_4_out, and_5_out, and_6_out, and_7_out, and_8_out, and_9_out,
       and_10_out, and_11_out, and_12_out, and_13_out, and_14_out, and_15_out, and_16_out, and_17_out,
       and_18_out, not_1_out, not_2_out, not_3_out, not_4_out, not_5_out, not_6_out, not_7_out, not_8_out,
       or_1_out, or_2_out, or_4_out, or_6_out;

  not not_1 (not_1_out, j11);
  not not_2 (not_2_out, j20);
  not not_3 (not_3_out, j21);
  and and_1 (and_1_out, j21, j20);
  not not_4 (not_4_out, j10);
  not not_5 (not_5_out, j10);
  not not_6 (not_6_out, j21);
  not not_7 (not_7_out, j11);
  not not_8 (not_8_out, j20);
  and and_2 (and_2_out, not_1_out, and_3_out);
  and and_3 (and_3_out, not_2_out, j21);
  and and_4 (and_4_out, j10, and_5_out);
  and and_5 (and_5_out, j20, not_3_out);
  and and_6 (and_6_out, j11, and_1_out);
  and and_7 (and_7_out, j11, and_8_out);
  and and_8 (and_8_out, not_4_out, j21);
  and and_9 (and_9_out, j11, and_10_out);
  and and_10 (and_10_out, j20, not_6_out);
  and and_11 (and_11_out, not_7_out, j20);
  and and_12 (and_12_out, and_11_out, j10);
  buf and_13 (and_13_out, j10);  // AND_Gate
  and and_14 (and_14_out, and_13_out, j11);
  and and_15 (and_15_out, j11, and_16_out);
  and and_16 (and_16_out, j21, not_8_out);
  and and_17 (and_17_out, j10, and_2_out);
  or or_1 (or_1_out, and_6_out, and_7_out);
  and and_18 (and_18_out, not_5_out, and_9_out);
  or or_2 (or_2_out, and_14_out, and_15_out);
  or or_3 (out_5, and_17_out, or_4_out);
  or or_4 (or_4_out, and_4_out, or_1_out);
  or or_5 (out_6, and_18_out, or_6_out);
  or or_6 (or_6_out, and_12_out, or_2_out);
endmodule

module cod (
  input  Te,
  input  Pa,
  input  Pe,
  output out_4,
  output out_5
);

  wire and_1_out, and_2_out, and_3_out, and_4_out, and_5_out, and_6_out, and_7_out, and_8_out, not_1_out,
       not_2_out, not_3_out, not_4_out, not_5_out, not_6_out, not_7_out, not_8_out;

  not not_1 (not_1_out, Te);
  and and_1 (and_1_out, Pa, not_2_out);
  not not_2 (not_2_out, Pe);
  not not_3 (not_3_out, Pa);
  and and_2 (and_2_out, not_3_out, not_4_out);
  not not_4 (not_4_out, Pe);
  not not_5 (not_5_out, Te);
  not not_6 (not_6_out, Pa);
  and and_3 (and_3_out, not_6_out, Pe);
  not not_7 (not_7_out, Pa);
  and and_4 (and_4_out, not_7_out, not_8_out);
  not not_8 (not_8_out, Pe);
  and and_5 (and_5_out, not_1_out, and_1_out);
  and and_6 (and_6_out, Te, and_2_out);
  and and_7 (and_7_out, not_5_out, and_3_out);
  and and_8 (and_8_out, Te, and_4_out);
  or or_1 (out_4, and_5_out, and_6_out);
  or or_2 (out_5, and_7_out, and_8_out);
endmodule

module dec (
  input  in_1,
  input  in_2,
  output J1,
  output J2,
  output EmpateOuInvalido
);

  wire and_3_out, and_4_out, not_1_out, not_2_out, not_3_out, not_4_out;

  not not_1 (not_1_out, in_2);
  not not_2 (not_2_out, in_1);
  not not_3 (not_3_out, in_1);
  not not_4 (not_4_out, in_2);
  and and_1 (J1, in_1, not_1_out);
  and and_2 (J2, not_2_out, in_2);
  and and_3 (and_3_out, not_3_out, not_4_out);
  and and_4 (and_4_out, in_1, in_2);
  or or_1 (EmpateOuInvalido, and_3_out, and_4_out);
endmodule
